# Fritzing sketch Power System (saved by Fritzing 0.9.4)

parts:
  Part3 = Adafruit PowerBoost 1000C [part_number="Adafruit #2465"]
  Part2 = INA 260
  Raspberry_Pi_1 = Raspberry Pi 3 [part_number=RPI-3-V1.2]
  VCC1 = Battery

nets:
  N1: Part3.VBUS, Raspberry_Pi_1.GPIO20
  N2: Part3.VLIPO, VCC1.+
  GND: Part3.GND, Part2.GND, Raspberry_Pi_1.GND, VCC1.-
  N3: Part3.LBO, Raspberry_Pi_1.GPIO21
  N4: Part3.5.0V, Part2.IN+
  N5: Part2.SCL, Raspberry_Pi_1.GPIO3
  N6: Part2.SDA, Raspberry_Pi_1.GPIO2
  N7: Part2.IN-, Raspberry_Pi_1.5V

custom parts:
  Adafruit PowerBoost 1000C: PowerBoost 1000C is the perfect power supply for your portable project! With a built-in load-sharing battery charger circuit, you'll be able to keep your power-hungry project running even while recharging the battery! This little DC/DC boost converter module can be powered by any 3.7V LiIon/LiPoly battery, and convert the battery output to 5.2V DC for running your 5V projects.
  INA 260: Rev. B, add copy
